# Fritzing sketch SR04_distance_display (saved by Fritzing 0.9.3b)
circuit board: 8.46667cm x 5.64444cm
breadboards: 1

parts:
  Bauteil1 = Arduino Uno (Rev3)
  R1 = Trimmer Potentiometer [maximum_resistance=10kΩ package=THT]
  LCD1 = LCD screen
  hc-sr1 = hc-sr04

nets:
  N1: Bauteil1.D8, LCD1.E
  N2: Bauteil1.D9_PWM, LCD1.DB4
  N3: Bauteil1.D10_PWM/SS, LCD1.DB5
  N4: Bauteil1.D11_PWM/MOSI, LCD1.DB6
  N5: Bauteil1.D12/MISO, LCD1.DB7
  GND: Bauteil1.GND, R1.leg2, LCD1.VSS, LCD1.R/W, LCD1.LED-, hc-sr1.GND
  N6: Bauteil1.D2, hc-sr1.Trig
  N7: Bauteil1.D3_PWM, hc-sr1.Echo
  N8: Bauteil1.D7, LCD1.RS
  5V: Bauteil1.5V, R1.leg1, LCD1.VDD, LCD1.LED+, hc-sr1.VCC
  N9: R1.wiper, LCD1.V0

// code stored in the sketch: SR04_distance_display.ino
//www.elegoo.com
//2016.12.9

#include <LiquidCrystal.h>
#include "SR04.h"

//                BS  E  D4 D5  D6 D7
LiquidCrystal lcd(7, 8, 9, 10, 11, 12);

//         ECHO_PIN TRIG_PIN
SR04 sr04 = SR04(3, 2);
long a;

void setup()
{
  lcd.begin(16, 2);
}

void loop()
{
  lcd.setCursor(0, 0);
  a = sr04.Distance();
  lcd.print("Distance    cm  ");
  lcd.setCursor(9, 0);
  lcd.print(a);
  delay(500);
}

// code stored in the sketch: Thermometer_v2.ino
//www.elegoo.com
//2016.12.9

#include <LiquidCrystal.h>
#include "SR04.h"

//                BS  E  D4 D5  D6 D7
LiquidCrystal lcd(7, 8, 9, 10, 11, 12);

//         ECHO_PIN TRIG_PIN
SR04 sr04 = SR04(3, 2);
long a;

void setup()
{
  lcd.begin(16, 2);
}

void loop()
{
  lcd.setCursor(0, 0);
  a = sr04.Distance();
  lcd.print("Distance    cm  ");
  lcd.setCursor(9, 0);
  lcd.print(a);
  delay(500);
}
